// Digital circuit CPU 8.dig as structural Verilog
module CPU_8 (
  input  Clock,
  input  RST,
  input  DMA,
  input  nWAIT,
  input  in_7,
  input  in_8,
  input  in_9,
  output CLK1,
  output CLK2
);

  wire and_1_out, and_2_out, and_6_out, and_9_out, and_10_out, and_11_out, and_12_out, and_13_out,
       and_14_out, and_17_out, COND_C, COND_N, COND_NEG, COND_POS, COND_RES, COND_Z, CONV_V,
       demultiplexer_1_out_0, demultiplexer_1_out_1, demultiplexer_2_out_1, demultiplexer_2_out_2,
       demultiplexer_2_out_3, demultiplexer_2_out_4, demultiplexer_2_out_5, demultiplexer_4_out_0,
       demultiplexer_4_out_1, demultiplexer_4_out_2, demultiplexer_5_out_1, demultiplexer_5_out_2,
       demultiplexer_5_out_3, demultiplexer_5_out_4, demultiplexer_5_out_5, demultiplexer_5_out_6,
       demultiplexer_5_out_7, demultiplexer_6_out_0, demultiplexer_6_out_1, demultiplexer_6_out_2,
       demultiplexer_6_out_3, demultiplexer_6_out_4, demultiplexer_6_out_5, demultiplexer_6_out_6,
       demultiplexer_6_out_7, demultiplexer_7_out_0, demultiplexer_7_out_1, demultiplexer_7_out_2,
       demultiplexer_8_out_1, demultiplexer_8_out_2, demultiplexer_8_out_3, demultiplexer_8_out_4,
       demultiplexer_8_out_5, demultiplexer_9_out_0, demultiplexer_9_out_1, demultiplexer_9_out_2,
       demultiplexer_9_out_3, demultiplexer_9_out_4, demultiplexer_9_out_5, demultiplexer_9_out_7,
       demultiplexer_10_out_0, demultiplexer_10_out_1, demultiplexer_10_out_2, demultiplexer_11_out_1,
       demultiplexer_11_out_2, demultiplexer_11_out_3, demultiplexer_11_out_4, demultiplexer_11_out_5,
       demultiplexer_11_out_6, demultiplexer_11_out_7, demultiplexer_12_out_0, demultiplexer_12_out_1,
       demultiplexer_12_out_2, demultiplexer_12_out_3, demultiplexer_12_out_4, demultiplexer_12_out_5,
       demultiplexer_12_out_6, demultiplexer_12_out_7, demultiplexer_13_out_0, demultiplexer_13_out_1,
       demultiplexer_14_out_1, demultiplexer_14_out_2, demultiplexer_14_out_3, demultiplexer_14_out_4,
       DMA_ack, FAULT_any, FLAG_C, FLAG_V, IRQ0_any, IRQ1_any, IRQ_ack, IRQ_DOUT, IRQ_en, IRQ_FTdat, IRQ_REQ,
       nA_ALUin, nA_DATout, nA_st, nB_DATout, nB_st, nBASE_st, nBIT_DATout, nC_DATout, nC_Fst, nC_st,
       nD_DATout, nD_st, nF_ALUin, nF_DATin, nF_DATout, nIR_st, nIRQ_DOUT, nIRQ_Fst, nIX_DATout, nIX_st,
       nIY_DATout, nIY_st, nLSH_DATout, nMAR_ADSout, nMARH_st, nMARL_st, nMEM_DATout, nMEM_st, nMSK_st,
       nNZ_Fst, nOFF_ADSout, nor_1_out, nor_2_out, nor_3_out, nor_4_out, nor_5_out, nor_6_out, nor_7_out,
       nor_8_out, nor_9_out, nor_10_out, nor_11_out, nor_12_out, nor_13_out, nor_14_out, nor_15_out,
       nor_16_out, not_1_out, not_2_out, not_3_out, not_4_out, not_5_out, not_22_out, not_23_out, not_24_out,
       not_26_out, not_27_out, not_40_out, not_41_out, not_42_out, not_43_out, not_44_out, not_45_out,
       not_46_out, not_47_out, not_48_out, not_59_out, not_70_out, not_71_out, nPC_ADSout, nPC_DATout,
       nPC_en, nPC_st, nREL_st, nRSH_DATout, nRST_ADSout, nSEQ_en, nSEQ_st, nSP_ADSout, nSP_DATout, nSP_en,
       nSP_st, nSUM_DATout, nSUM_st, nTMEM_out, nTMEM_st, nV_Fst, nWORD_DATout, or_4_out, or_5_out, or_6_out,
       or_7_out, or_9_out, or_10_out, or_11_out, or_12_out, or_13_out, SEQ_val, SP_dir, t_ff_1_nq, t_ff_1_q,
       TEMP_clr, \Σ_Csel , \Σ_Cval , \Σ_M ;
  wire [1:0] FLAG_NZ;
  wire [2:0] AOUT_sel, COND_sel, driverinvsel_4_out, driverinvsel_5_out, FAULT_num, IRQ0_num, IRQ1_num,
       or_1_out;
  wire [3:0] alu_1_c_f, driverinvsel_18_out, FST_sel, \µSEQ_out , \Σ_sel ;
  wire [4:0] DOUT_sel, ST_sel;
  wire [6:4] DMA_q, not_7_out;
  wire [7:0] MARH_out, MARL_out, MSK_2_q, MSK_q;
  wire [9:0] IR_q;
  wire [15:0] A_q, ADDRESS_in, ADDRESS_out, alu_1_sum, B_q, barrelshifter_1_out, barrelshifter_2_out,
       BASE_out, C_q, D_q, DATA_in, DATA_out, driverinvsel_11_out, IX_out, IY_out, OFFSET_s, PC_out, REL_out,
       ROM_16x64k_d, SP_out, SUM_out, TMEM_out;
  wire [47:0] \µCODE_d ;
  wire [47:29] CTRL_q;

  Demultiplexer demultiplexer_1 (
    .sel(FST_sel[3]), .in(1'b1), .out_0(demultiplexer_1_out_0), .out_1(demultiplexer_1_out_1));
  assign ADDRESS_out = ~nRST_ADSout ? {16{1'b1}} : 16'bz;  // DriverInvSel driverinvsel_1
  assign DATA_out = ~nWORD_DATout ? {16{1'b1}} : 16'bz;  // DriverInvSel driverinvsel_2
  assign DATA_out = ~nBIT_DATout ? 16'h1 : 16'bz;  // DriverInvSel driverinvsel_3
  Register #(.Bits(8)) MSK (.D(DATA_in[7:0]), .C(CLK2), .en(~nMSK_st), .Q(MSK_q));
  Register #(.Bits(8)) MSK_2 (.D(DATA_in[7:0]), .C(CLK2), .en(~nMSK_st), .Q(MSK_2_q));
  not not_1 (not_1_out, COND_RES);
  Register IRQ (.D(DATA_in[4]), .C(CLK2), .en(~nIRQ_Fst), .Q(IRQ_FTdat));
  Demultiplexer #(.Selector_Bits(3)) demultiplexer_2 (
    .sel(FST_sel[2:0]), .in(demultiplexer_1_out_0), .out_1(demultiplexer_2_out_1),
    .out_2(demultiplexer_2_out_2), .out_3(demultiplexer_2_out_3), .out_4(demultiplexer_2_out_4),
    .out_5(demultiplexer_2_out_5));  // open: out_0, out_6, out_7
  Demultiplexer #(.Selector_Bits(3)) demultiplexer_3 (
    .sel(FST_sel[2:0]), .in(demultiplexer_1_out_1));  // open: out_0, out_1, out_2, out_3, out_4, out_5, out_6, out_7
  and and_1 (and_1_out, nSEQ_st, not_1_out);
  not not_2 (not_2_out, demultiplexer_2_out_1);
  not not_3 (not_3_out, demultiplexer_2_out_2);
  not not_4 (not_4_out, demultiplexer_2_out_3);
  not not_5 (not_5_out, demultiplexer_2_out_4);
  not not_6 (nIRQ_Fst, demultiplexer_2_out_5);
  and and_2 (and_2_out, IRQ_REQ, IRQ_FTdat);
  PullDown #(.Bits(16)) pulldown_1 (.out(ADDRESS_out));
  PullDown #(.Bits(16)) pulldown_2 (.out(DATA_out));
  PullDown #(.Bits(16)) pulldown_3 (.out(DATA_out));
  and and_3 (nNZ_Fst, not_2_out, not_5_out);
  and and_4 (nV_Fst, not_3_out, not_5_out);
  and and_5 (nC_Fst, not_4_out, not_5_out);
  nor nor_1 (nor_1_out, MSK_q[0], 1'b0);
  nor nor_2 (nor_2_out, MSK_q[1], 1'b0);
  nor nor_3 (nor_3_out, MSK_q[2], 1'b0);
  nor nor_4 (nor_4_out, MSK_q[3], 1'b0);
  nor nor_5 (nor_5_out, MSK_q[4], 1'b0);
  nor nor_6 (nor_6_out, MSK_q[5], 1'b0);
  nor nor_7 (nor_7_out, MSK_q[6], 1'b0);
  nor nor_8 (nor_8_out, MSK_q[7], 1'b0);
  nor nor_9 (nor_9_out, MSK_2_q[0], 1'b0);
  nor nor_10 (nor_10_out, MSK_2_q[1], 1'b0);
  nor nor_11 (nor_11_out, MSK_2_q[2], 1'b0);
  nor nor_12 (nor_12_out, MSK_2_q[3], 1'b0);
  nor nor_13 (nor_13_out, MSK_2_q[4], 1'b0);
  nor nor_14 (nor_14_out, MSK_2_q[5], 1'b0);
  nor nor_15 (nor_15_out, MSK_2_q[6], 1'b0);
  nor nor_16 (nor_16_out, MSK_2_q[7], 1'b0);
  CounterPreset #(.Bits(4)) \u_µSEQ  (
    .en(~nSEQ_en), .C(CLK2), .dir(1'b0), .in({3'b000, SEQ_val}), .ld(~and_1_out), .clr(1'b0), .out(\µSEQ_out ));  // open: ovf
  Register u_DMA (.D(DMA), .C(CLK2), .en(~IRQ_en), .Q(DMA_q[4]));
  Register RESET (.D(RST), .C(CLK2), .en(~IRQ_en), .Q(DMA_q[5]));
  Register IRQ_2 (.D(and_2_out), .C(CLK2), .en(~IRQ_en), .Q(DMA_q[6]));
  Register #(.Bits(10)) IR (.D(DATA_in[9:0]), .C(CLK2), .en(~nIR_st), .Q(IR_q));
  PriorityEncoder #(.Selector_Bits(3)) FAULT (
    .in0(1'b0), .in1(1'b0), .in2(1'b0), .in3(1'b0), .in4(1'b0), .in5(1'b0), .in6(1'b0), .in7(1'b0),
    .num(FAULT_num), .any(FAULT_any));
  PriorityEncoder #(.Selector_Bits(3)) IRQ0 (
    .in0(nor_1_out), .in1(nor_2_out), .in2(nor_3_out), .in3(nor_4_out), .in4(nor_5_out), .in5(nor_6_out),
    .in6(nor_7_out), .in7(nor_8_out), .num(IRQ0_num), .any(IRQ0_any));
  PriorityEncoder #(.Selector_Bits(3)) IRQ1 (
    .in0(nor_9_out), .in1(nor_10_out), .in2(nor_11_out), .in3(nor_12_out), .in4(nor_13_out),
    .in5(nor_14_out), .in6(nor_15_out), .in7(nor_16_out), .num(IRQ1_num), .any(IRQ1_any));
  not not_7 (not_7_out[4], FAULT_any);
  not not_8 (not_7_out[5], IRQ0_any);
  not not_9 (not_7_out[6], IRQ1_any);
  ROM #(.AddrBits(17), .Bits(48)) \u_µCODE  (.A({IR_q, DMA_q, \µSEQ_out }), .sel(1'b1), .D(\µCODE_d ));
  Demultiplexer #(.Selector_Bits(2)) demultiplexer_4 (
    .sel(ST_sel[4:3]), .in(1'b1), .out_0(demultiplexer_4_out_0), .out_1(demultiplexer_4_out_1),
    .out_2(demultiplexer_4_out_2));  // open: out_3
  assign driverinvsel_4_out = ~not_7_out[4] ? IRQ0_num : 3'bz;  // DriverInvSel driverinvsel_4
  assign driverinvsel_5_out = ~and_6_out ? IRQ1_num : 3'bz;  // DriverInvSel driverinvsel_5
  D_FF #(.Bits(48)) CTRL (
    .D(\µCODE_d ), .C(CLK1),
    .Q({CTRL_q[47:40], nA_ALUin, IRQ_ack, DMA_ack, CTRL_q[36], TEMP_clr, SEQ_val, CTRL_q[33:32], nF_ALUin, CTRL_q[30:29], SP_dir, COND_POS, \Σ_Cval , \Σ_Csel , \Σ_M , \Σ_sel , COND_sel, FST_sel, AOUT_sel, DOUT_sel, ST_sel}));  // open: nQ
  Demultiplexer #(.Selector_Bits(3)) demultiplexer_5 (
    .sel(ST_sel[2:0]), .in(demultiplexer_4_out_0), .out_1(demultiplexer_5_out_1),
    .out_2(demultiplexer_5_out_2), .out_3(demultiplexer_5_out_3), .out_4(demultiplexer_5_out_4),
    .out_5(demultiplexer_5_out_5), .out_6(demultiplexer_5_out_6), .out_7(demultiplexer_5_out_7));  // open: out_0
  Demultiplexer #(.Selector_Bits(3)) demultiplexer_6 (
    .sel(ST_sel[2:0]), .in(demultiplexer_4_out_1), .out_0(demultiplexer_6_out_0),
    .out_1(demultiplexer_6_out_1), .out_2(demultiplexer_6_out_2), .out_3(demultiplexer_6_out_3),
    .out_4(demultiplexer_6_out_4), .out_5(demultiplexer_6_out_5), .out_6(demultiplexer_6_out_6),
    .out_7(demultiplexer_6_out_7));
  Demultiplexer #(.Selector_Bits(3)) demultiplexer_7 (
    .sel(ST_sel[2:0]), .in(demultiplexer_4_out_2), .out_0(demultiplexer_7_out_0),
    .out_1(demultiplexer_7_out_1), .out_2(demultiplexer_7_out_2));  // open: out_3, out_4, out_5, out_6, out_7
  Demultiplexer #(.Selector_Bits(3)) demultiplexer_8 (
    .sel(AOUT_sel), .in(1'b1), .out_1(demultiplexer_8_out_1), .out_2(demultiplexer_8_out_2),
    .out_3(demultiplexer_8_out_3), .out_4(demultiplexer_8_out_4), .out_5(demultiplexer_8_out_5));  // open: out_0, out_6, out_7
  and and_6 (and_6_out, not_7_out[4], not_7_out[5]);
  not not_10 (nA_st, demultiplexer_5_out_1);
  not not_11 (nB_st, demultiplexer_5_out_2);
  not not_12 (nC_st, demultiplexer_5_out_3);
  not not_13 (nD_st, demultiplexer_5_out_4);
  not not_14 (nSP_st, demultiplexer_5_out_5);
  not not_15 (nPC_st, demultiplexer_5_out_6);
  not not_16 (nIX_st, demultiplexer_5_out_7);
  not not_17 (nIY_st, demultiplexer_6_out_0);
  not not_18 (nIR_st, demultiplexer_6_out_1);
  not not_19 (nREL_st, demultiplexer_6_out_2);
  not not_20 (nBASE_st, demultiplexer_6_out_3);
  not not_21 (nSUM_st, demultiplexer_6_out_4);
  not not_22 (not_22_out, demultiplexer_6_out_5);
  not not_23 (not_23_out, demultiplexer_6_out_6);
  not not_24 (not_24_out, demultiplexer_6_out_7);
  not not_25 (nMSK_st, demultiplexer_7_out_0);
  not not_26 (not_26_out, demultiplexer_7_out_1);
  not not_27 (not_27_out, demultiplexer_7_out_2);
  not not_28 (nSP_ADSout, demultiplexer_8_out_1);
  not not_29 (nPC_ADSout, demultiplexer_8_out_2);
  not not_30 (nOFF_ADSout, demultiplexer_8_out_3);
  not not_31 (nMAR_ADSout, demultiplexer_8_out_4);
  not not_32 (nRST_ADSout, demultiplexer_8_out_5);
  not not_33 (nSP_en, CTRL_q[29]);
  not not_34 (nPC_en, CTRL_q[30]);
  not not_35 (nSEQ_en, CTRL_q[32]);
  not not_36 (nSEQ_st, CTRL_q[33]);
  not not_37 (IRQ_en, CTRL_q[36]);
  assign or_1_out = FAULT_num | driverinvsel_4_out | driverinvsel_5_out;  // Or or_1, 3 bits wide
  and and_7 (nMARH_st, not_22_out, not_26_out);
  and and_8 (nMARL_st, not_27_out, not_22_out);
  not not_38 (COND_NEG, COND_POS);
  not not_39 (nF_DATin, nF_ALUin);
  Demultiplexer #(.Selector_Bits(3)) demultiplexer_9 (
    .sel(ADDRESS_in[15:13]), .in(1'b1), .out_0(demultiplexer_9_out_0), .out_1(demultiplexer_9_out_1),
    .out_2(demultiplexer_9_out_2), .out_3(demultiplexer_9_out_3), .out_4(demultiplexer_9_out_4),
    .out_5(demultiplexer_9_out_5), .out_7(demultiplexer_9_out_7));  // open: out_6
  not not_40 (not_40_out, demultiplexer_9_out_0);
  not not_41 (not_41_out, demultiplexer_9_out_1);
  not not_42 (not_42_out, demultiplexer_9_out_2);
  not not_43 (not_43_out, demultiplexer_9_out_3);
  not not_44 (not_44_out, demultiplexer_9_out_4);
  not not_45 (not_45_out, demultiplexer_9_out_5);
  not not_46 (not_46_out, demultiplexer_9_out_7);
  and and_9 (and_9_out, DMA_ack, in_8);
  and and_10 (and_10_out, in_9, DMA_ack);
  DriverInvSel #(.Bits(3)) driverinvsel_6 (.in(or_1_out), .en(IRQ_DOUT));  // open: out
  and and_11 (and_11_out, ~COND_N, FLAG_NZ[0]);  // And
  or or_2 (nMEM_st, and_9_out, not_23_out);
  or or_3 (nTMEM_st, not_24_out, and_10_out);
  and and_12 (and_12_out, ~COND_Z, FLAG_NZ[1]);  // And
  or or_4 (or_4_out, not_40_out, not_41_out, not_42_out, not_43_out, not_44_out, not_45_out);
  and and_13 (and_13_out, ~CONV_V, FLAG_V);  // And
  not not_47 (not_47_out, Clock);
  PullDown pulldown_4 (.out(Clock));
  or or_5 (or_5_out, and_11_out, and_12_out);
  and and_14 (and_14_out, ~COND_C, ~FLAG_C);  // And
  T_FF #(.withEnable("false")) t_ff_1 (.C(not_47_out), .Q(t_ff_1_q), .nQ(t_ff_1_nq));
  or or_6 (or_6_out, and_13_out, and_14_out);
  and and_15 (CLK1, Clock, t_ff_1_q);
  and and_16 (CLK2, t_ff_1_nq, ~nWAIT, Clock);  // And
  Demultiplexer #(.Selector_Bits(2)) demultiplexer_10 (
    .sel(DOUT_sel[4:3]), .in(1'b1), .out_0(demultiplexer_10_out_0), .out_1(demultiplexer_10_out_1),
    .out_2(demultiplexer_10_out_2));  // open: out_3
  ROM #(.AddrBits(16), .Bits(16)) ROM_16x64k (.A(ADDRESS_in), .sel(not_48_out), .D(ROM_16x64k_d));
  not not_48 (not_48_out, not_46_out);
  RAMSinglePortSel #(.AddrBits(16), .Bits(16)) RAM0_16x64k (
    .A(ADDRESS_in), .CS(~or_4_out), .WE(~nMEM_st), .OE(~nMEM_DATout), .D(ROM_16x64k_d));
  Demultiplexer #(.Selector_Bits(3)) demultiplexer_11 (
    .sel(DOUT_sel[2:0]), .in(demultiplexer_10_out_0), .out_1(demultiplexer_11_out_1),
    .out_2(demultiplexer_11_out_2), .out_3(demultiplexer_11_out_3), .out_4(demultiplexer_11_out_4),
    .out_5(demultiplexer_11_out_5), .out_6(demultiplexer_11_out_6), .out_7(demultiplexer_11_out_7));  // open: out_0
  Demultiplexer #(.Selector_Bits(3)) demultiplexer_12 (
    .sel(DOUT_sel[2:0]), .in(demultiplexer_10_out_1), .out_0(demultiplexer_12_out_0),
    .out_1(demultiplexer_12_out_1), .out_2(demultiplexer_12_out_2), .out_3(demultiplexer_12_out_3),
    .out_4(demultiplexer_12_out_4), .out_5(demultiplexer_12_out_5), .out_6(demultiplexer_12_out_6),
    .out_7(demultiplexer_12_out_7));
  Demultiplexer #(.Selector_Bits(3)) demultiplexer_13 (
    .sel(DOUT_sel[2:0]), .in(demultiplexer_10_out_2), .out_0(demultiplexer_13_out_0),
    .out_1(demultiplexer_13_out_1));  // open: out_2, out_3, out_4, out_5, out_6, out_7
  Demultiplexer #(.Selector_Bits(3)) demultiplexer_14 (
    .sel(COND_sel), .in(1'b1), .out_1(demultiplexer_14_out_1), .out_2(demultiplexer_14_out_2),
    .out_3(demultiplexer_14_out_3), .out_4(demultiplexer_14_out_4));  // open: out_0, out_5, out_6, out_7
  or or_7 (or_7_out, or_5_out, or_6_out);
  not not_49 (nA_DATout, demultiplexer_11_out_1);
  not not_50 (nB_DATout, demultiplexer_11_out_2);
  not not_51 (nC_DATout, demultiplexer_11_out_3);
  not not_52 (nD_DATout, demultiplexer_11_out_4);
  not not_53 (nSP_DATout, demultiplexer_11_out_5);
  not not_54 (nPC_DATout, demultiplexer_11_out_6);
  not not_55 (nIX_DATout, demultiplexer_11_out_7);
  not not_56 (nIY_DATout, demultiplexer_12_out_0);
  not not_57 (nF_DATout, demultiplexer_12_out_1);
  not not_58 (nSUM_DATout, demultiplexer_12_out_2);
  not not_59 (not_59_out, demultiplexer_12_out_3);
  not not_60 (nLSH_DATout, demultiplexer_12_out_4);
  not not_61 (nRSH_DATout, demultiplexer_12_out_5);
  not not_62 (nWORD_DATout, demultiplexer_12_out_6);
  not not_63 (nBIT_DATout, demultiplexer_12_out_7);
  not not_64 (nTMEM_out, demultiplexer_13_out_0);
  not not_65 (nIRQ_DOUT, demultiplexer_13_out_1);
  not not_66 (COND_N, demultiplexer_14_out_1);
  not not_67 (COND_Z, demultiplexer_14_out_2);
  not not_68 (CONV_V, demultiplexer_14_out_3);
  not not_69 (COND_C, demultiplexer_14_out_4);
  PullDown #(.Bits(16)) pulldown_5 (.out(ROM_16x64k_d));
  not not_70 (not_70_out, or_7_out);
  assign ROM_16x64k_d = ~nTMEM_out ? TMEM_out : 16'bz;  // DriverInvSel driverinvsel_7
  assign COND_RES = ~COND_POS ? or_7_out : 1'bz;  // DriverInvSel driverinvsel_8
  assign COND_RES = ~COND_NEG ? not_70_out : 1'bz;  // DriverInvSel driverinvsel_9
  and and_17 (and_17_out, DMA_ack, in_7);
  assign DATA_out = ~nMEM_DATout ? ROM_16x64k_d : 16'bz;  // DriverInvSel driverinvsel_10
  or or_8 (nMEM_DATout, and_17_out, not_59_out);
  CounterPreset #(.Bits(16)) TMEM (
    .en(~1'b1), .C(CLK2), .dir(1'b0), .in(DATA_in), .ld(~nTMEM_st), .clr(TEMP_clr), .out(TMEM_out));  // open: ovf
  LED D15 (.in(DATA_in[15]));
  LED A15 (.in(ADDRESS_in[15]));
  Register #(.Bits(16)) A (.D(DATA_in), .C(CLK2), .en(~nA_st), .Q(A_q));
  LED D13 (.in(DATA_in[13]));
  LED D14 (.in(DATA_in[14]));
  LED A13 (.in(ADDRESS_in[13]));
  LED A14 (.in(ADDRESS_in[14]));
  assign driverinvsel_11_out = ~nA_ALUin ? A_q : 16'bz;  // DriverInvSel driverinvsel_11
  Register #(.Bits(16)) B (.D(DATA_in), .C(CLK2), .en(~nB_st), .Q(B_q));
  Register #(.Bits(16)) C (.D(DATA_in), .C(CLK2), .en(~nC_st), .Q(C_q));
  Register #(.Bits(16)) D (.D(DATA_in), .C(CLK2), .en(~nD_st), .Q(D_q));
  CounterPreset #(.Bits(16)) IX (
    .en(~1'b1), .C(CLK2), .dir(1'b0), .in(DATA_in), .ld(~nB_st), .clr(1'b0), .out(IX_out));  // open: ovf
  CounterPreset #(.Bits(16)) IY (
    .en(~1'b1), .C(CLK2), .dir(1'b0), .in(DATA_in), .ld(~nB_st), .clr(1'b0), .out(IY_out));  // open: ovf
  LED D12 (.in(DATA_in[12]));
  LED A12 (.in(ADDRESS_in[12]));
  PullDown #(.Bits(16)) pulldown_6 (.out(driverinvsel_11_out));
  LED D11 (.in(DATA_in[11]));
  LED A11 (.in(ADDRESS_in[11]));
  assign DATA_out = ~nA_DATout ? driverinvsel_11_out : 16'bz;  // DriverInvSel driverinvsel_12
  assign DATA_out = ~nB_DATout ? B_q : 16'bz;  // DriverInvSel driverinvsel_13
  assign DATA_out = ~nC_DATout ? C_q : 16'bz;  // DriverInvSel driverinvsel_14
  assign DATA_out = ~nD_DATout ? D_q : 16'bz;  // DriverInvSel driverinvsel_15
  assign DATA_out = ~nIX_DATout ? IX_out : 16'bz;  // DriverInvSel driverinvsel_16
  assign DATA_out = ~nIY_DATout ? IY_out : 16'bz;  // DriverInvSel driverinvsel_17
  LED D9 (.in(DATA_in[9]));
  LED D10 (.in(DATA_in[10]));
  LED A9 (.in(ADDRESS_in[9]));
  LED A10 (.in(ADDRESS_in[10]));
  PullDown #(.Bits(16)) pulldown_7 (.out(DATA_out));
  LED D8 (.in(DATA_in[8]));
  LED A8 (.in(ADDRESS_in[8]));
  PullDown #(.Bits(16)) pulldown_8 (.out(DATA_out));
  PullDown #(.Bits(16)) pulldown_9 (.out(DATA_out));
  PullDown #(.Bits(16)) pulldown_10 (.out(DATA_out));
  PullDown #(.Bits(16)) pulldown_11 (.out(DATA_out));
  PullDown #(.Bits(16)) pulldown_12 (.out(DATA_out));
  LED D7 (.in(DATA_in[7]));
  LED A7 (.in(ADDRESS_in[7]));
  LED D5 (.in(DATA_in[5]));
  LED D6 (.in(DATA_in[6]));
  LED A5 (.in(ADDRESS_in[5]));
  LED A6 (.in(ADDRESS_in[6]));
  ALU alu_1 (
    .Sum(alu_1_sum), .C_sel(\Σ_Csel ), .C_val(\Σ_Cval ), .nCin(FLAG_C), .A(driverinvsel_11_out),
    .Sel(\Σ_sel ), .B(DATA_in), .M(\Σ_M ), .C_f(alu_1_c_f[3]), .N_f(alu_1_c_f[2]), .Z_f(alu_1_c_f[1]),
    .V_f(alu_1_c_f[0]));
  LED D4 (.in(DATA_in[4]));
  LED A4 (.in(ADDRESS_in[4]));
  or or_9 (or_9_out, CLK2, TEMP_clr);
  assign driverinvsel_18_out = ~nF_DATin ? DATA_in[3:0] : 4'bz;  // DriverInvSel driverinvsel_18
  or or_10 (or_10_out, CLK2, TEMP_clr);
  or or_11 (or_11_out, CLK2, TEMP_clr);
  LED D3 (.in(DATA_in[3]));
  LED A3 (.in(ADDRESS_in[3]));
  assign driverinvsel_18_out = ~nF_ALUin ? alu_1_c_f : 4'bz;  // DriverInvSel driverinvsel_19
  LED D1 (.in(DATA_in[1]));
  LED D2 (.in(DATA_in[2]));
  LED A1 (.in(ADDRESS_in[1]));
  LED A2 (.in(ADDRESS_in[2]));
  CounterPreset #(.Bits(16)) SUM (
    .en(~1'b1), .C(or_9_out), .dir(1'b0), .in(alu_1_sum), .ld(~nSUM_st), .clr(TEMP_clr), .out(SUM_out));  // open: ovf
  PullDown #(.Bits(4)) pulldown_13 (.out(driverinvsel_18_out));
  CounterPreset #(.Bits(16)) PC (
    .en(~nPC_en), .C(CLK2), .dir(1'b0), .in(DATA_in), .ld(~nPC_st), .clr(1'b0), .out(PC_out));  // open: ovf
  CounterPreset #(.Bits(16)) SP (
    .en(~nSP_en), .C(CLK2), .dir(SP_dir), .in(DATA_in), .ld(~nSP_st), .clr(1'b0), .out(SP_out));  // open: ovf
  CounterPreset #(.Bits(8)) MARH (
    .en(~1'b1), .C(or_10_out), .dir(1'b0), .in(DATA_in[15:8]), .ld(~nMARH_st), .clr(TEMP_clr), .out(MARH_out));  // open: ovf
  CounterPreset #(.Bits(8)) MARL (
    .en(~1'b1), .C(or_11_out), .dir(1'b0), .in(DATA_in[7:0]), .ld(~nMARL_st), .clr(TEMP_clr), .out(MARL_out));  // open: ovf
  LED D0 (.in(DATA_in[0]));
  LED A0 (.in(ADDRESS_in[0]));
  assign DATA_out = ~nSUM_DATout ? SUM_out : 16'bz;  // DriverInvSel driverinvsel_20
  Register #(.Bits(2)) NZ_F (.D(driverinvsel_18_out[1:0]), .C(CLK2), .en(~nNZ_Fst), .Q(FLAG_NZ));
  Register V_F (.D(driverinvsel_18_out[2]), .C(CLK2), .en(~nV_Fst), .Q(FLAG_V));
  Register nC_F (.D(driverinvsel_18_out[3]), .C(CLK2), .en(~nC_Fst), .Q(FLAG_C));
  assign ADDRESS_out = ~nPC_ADSout ? PC_out : 16'bz;  // DriverInvSel driverinvsel_21
  assign DATA_out = ~nPC_DATout ? PC_out : 16'bz;  // DriverInvSel driverinvsel_22
  assign ADDRESS_out = ~nSP_ADSout ? SP_out : 16'bz;  // DriverInvSel driverinvsel_23
  assign DATA_out = ~nSP_DATout ? SP_out : 16'bz;  // DriverInvSel driverinvsel_24
  LED V (.in(FLAG_V));
  LED C_2 (.in(not_71_out));
  not not_71 (not_71_out, FLAG_C);
  assign ADDRESS_out = ~nMAR_ADSout ? {MARH_out, MARL_out} : 16'bz;  // DriverInvSel driverinvsel_25
  LED Z (.in(FLAG_NZ[1]));
  PullDown #(.Bits(16)) pulldown_14 (.out(DATA_out));
  PullDown #(.Bits(16)) pulldown_15 (.out(DATA_out));
  PullDown #(.Bits(16)) pulldown_16 (.out(ADDRESS_out));
  LED N (.in(FLAG_NZ[0]));
  PullDown #(.Bits(16)) pulldown_17 (.out(ADDRESS_out));
  PullDown #(.Bits(16)) pulldown_18 (.out(ADDRESS_out));
  PullDown #(.Bits(16)) pulldown_19 (.out(DATA_out));
  assign DATA_out = ~nF_DATout ? {{11{1'b0}}, IRQ_FTdat, FLAG_C, FLAG_V, FLAG_NZ} : 16'bz;  // DriverInvSel driverinvsel_26
  PullDown #(.Bits(16)) pulldown_20 (.out(DATA_out));
  or or_12 (or_12_out, CLK2, TEMP_clr);
  or or_13 (or_13_out, CLK2, TEMP_clr);
  CounterPreset #(.Bits(16)) REL (
    .en(~1'b1), .C(or_12_out), .dir(1'b0), .in(DATA_in), .ld(~nREL_st), .clr(TEMP_clr), .out(REL_out));  // open: ovf
  CounterPreset #(.Bits(16)) BASE (
    .en(~1'b1), .C(or_13_out), .dir(1'b0), .in(DATA_in), .ld(~nBASE_st), .clr(TEMP_clr), .out(BASE_out));  // open: ovf
  DiodeForward diodeforward_1 (.in(ADDRESS_out[0]), .out(ADDRESS_in[0]));
  DiodeForward diodeforward_2 (.in(ADDRESS_out[1]), .out(ADDRESS_in[1]));
  DiodeForward diodeforward_3 (.in(ADDRESS_out[2]), .out(ADDRESS_in[2]));
  DiodeForward diodeforward_4 (.in(ADDRESS_out[3]), .out(ADDRESS_in[3]));
  DiodeForward diodeforward_5 (.in(ADDRESS_out[4]), .out(ADDRESS_in[4]));
  DiodeForward diodeforward_6 (.in(ADDRESS_out[5]), .out(ADDRESS_in[5]));
  DiodeForward diodeforward_7 (.in(ADDRESS_out[6]), .out(ADDRESS_in[6]));
  DiodeForward diodeforward_8 (.in(ADDRESS_out[7]), .out(ADDRESS_in[7]));
  DiodeForward diodeforward_9 (.in(ADDRESS_out[8]), .out(ADDRESS_in[8]));
  DiodeForward diodeforward_10 (.in(ADDRESS_out[9]), .out(ADDRESS_in[9]));
  DiodeForward diodeforward_11 (.in(ADDRESS_out[10]), .out(ADDRESS_in[10]));
  DiodeForward diodeforward_12 (.in(ADDRESS_out[11]), .out(ADDRESS_in[11]));
  DiodeForward diodeforward_13 (.in(ADDRESS_out[12]), .out(ADDRESS_in[12]));
  DiodeForward diodeforward_14 (.in(ADDRESS_out[13]), .out(ADDRESS_in[13]));
  DiodeForward diodeforward_15 (.in(ADDRESS_out[14]), .out(ADDRESS_in[14]));
  DiodeForward diodeforward_16 (.in(ADDRESS_out[15]), .out(ADDRESS_in[15]));
  DiodeForward diodeforward_17 (.in(DATA_out[0]), .out(DATA_in[0]));
  DiodeForward diodeforward_18 (.in(DATA_out[1]), .out(DATA_in[1]));
  DiodeForward diodeforward_19 (.in(DATA_out[2]), .out(DATA_in[2]));
  DiodeForward diodeforward_20 (.in(DATA_out[3]), .out(DATA_in[3]));
  DiodeForward diodeforward_21 (.in(DATA_out[4]), .out(DATA_in[4]));
  DiodeForward diodeforward_22 (.in(DATA_out[5]), .out(DATA_in[5]));
  DiodeForward diodeforward_23 (.in(DATA_out[6]), .out(DATA_in[6]));
  DiodeForward diodeforward_24 (.in(DATA_out[7]), .out(DATA_in[7]));
  DiodeForward diodeforward_25 (.in(DATA_out[8]), .out(DATA_in[8]));
  DiodeForward diodeforward_26 (.in(DATA_out[9]), .out(DATA_in[9]));
  DiodeForward diodeforward_27 (.in(DATA_out[10]), .out(DATA_in[10]));
  DiodeForward diodeforward_28 (.in(DATA_out[11]), .out(DATA_in[11]));
  DiodeForward diodeforward_29 (.in(DATA_out[12]), .out(DATA_in[12]));
  DiodeForward diodeforward_30 (.in(DATA_out[13]), .out(DATA_in[13]));
  DiodeForward diodeforward_31 (.in(DATA_out[14]), .out(DATA_in[14]));
  DiodeForward diodeforward_32 (.in(DATA_out[15]), .out(DATA_in[15]));
  Add #(.Bits(16)) OFFSET (.a(REL_out), .b(BASE_out), .c_i(1'b0), .s(OFFSET_s));  // open: c_o
  BarrelShifter #(.Bits(16)) barrelshifter_1 (.in(BASE_out), .shift(5'b00001), .out(barrelshifter_1_out));
  BarrelShifter #(.Bits(16), .direction("right")) barrelshifter_2 (
    .in(BASE_out), .shift(5'b00001), .out(barrelshifter_2_out));
  PullDown pulldown_21 (.out(ADDRESS_in[15]));
  PullDown pulldown_22 (.out(ADDRESS_in[14]));
  PullDown pulldown_23 (.out(ADDRESS_in[13]));
  PullDown pulldown_24 (.out(DATA_in[15]));
  PullDown pulldown_25 (.out(DATA_in[14]));
  PullDown pulldown_26 (.out(DATA_in[13]));
  PullDown pulldown_27 (.out(ADDRESS_in[12]));
  PullDown pulldown_28 (.out(ADDRESS_in[11]));
  PullDown pulldown_29 (.out(ADDRESS_in[10]));
  PullDown pulldown_30 (.out(ADDRESS_in[9]));
  PullDown pulldown_31 (.out(DATA_in[12]));
  PullDown pulldown_32 (.out(DATA_in[11]));
  PullDown pulldown_33 (.out(DATA_in[10]));
  PullDown pulldown_34 (.out(DATA_in[9]));
  PullDown pulldown_35 (.out(ADDRESS_in[7]));
  PullDown pulldown_36 (.out(ADDRESS_in[6]));
  PullDown pulldown_37 (.out(ADDRESS_in[5]));
  PullDown pulldown_38 (.out(ADDRESS_in[8]));
  PullDown pulldown_39 (.out(DATA_in[7]));
  PullDown pulldown_40 (.out(DATA_in[6]));
  PullDown pulldown_41 (.out(DATA_in[5]));
  PullDown pulldown_42 (.out(DATA_in[8]));
  assign ADDRESS_out = ~nOFF_ADSout ? OFFSET_s : 16'bz;  // DriverInvSel driverinvsel_27
  assign DATA_out = ~nLSH_DATout ? barrelshifter_1_out : 16'bz;  // DriverInvSel driverinvsel_28
  assign DATA_out = ~nRSH_DATout ? barrelshifter_2_out : 16'bz;  // DriverInvSel driverinvsel_29
  PullDown pulldown_43 (.out(ADDRESS_in[4]));
  PullDown pulldown_44 (.out(ADDRESS_in[3]));
  PullDown pulldown_45 (.out(ADDRESS_in[2]));
  PullDown pulldown_46 (.out(ADDRESS_in[1]));
  PullDown pulldown_47 (.out(DATA_in[4]));
  PullDown pulldown_48 (.out(DATA_in[3]));
  PullDown pulldown_49 (.out(DATA_in[2]));
  PullDown pulldown_50 (.out(DATA_in[1]));
  PullDown #(.Bits(16)) pulldown_51 (.out(ADDRESS_out));
  PullDown #(.Bits(16)) pulldown_52 (.out(DATA_out));
  PullDown #(.Bits(16)) pulldown_53 (.out(DATA_out));
  PullDown pulldown_54 (.out(ADDRESS_in[0]));
  PullDown pulldown_55 (.out(DATA_in[0]));
  // Pins of 3 and 8 bits meet at {1'b0, not_7_out, 1'b0, or_1_out}

  // Other names for the same wires on the sheet: CLK_1 = CLK1; CLK_2 = CLK2

  // Notes on the sheet:
  //   Clock: Hz: 10
  //   RST: default 1
  //   DMA: default 1
  //   Control Sequencing
  //   Control Decoding
  //   Memory/IRQ
  //   contents of µCODE (hex, n*v repeats v):
  //   1900000969,1800081c0,100001566,20000a000,0,0,0,0,0,0,0,0,0,0,0,0,3000000000,3000000000,
  //   3000000000,3000000000,3000000000,3000000000,3000000000,3000000000,3000000000,3000000000,
  //   3000000000,3000000000,3000000000,3000000000,3000000000,3000000000,1900000969,1800081c0,
  //   100001566,20000a000,0,0,0,0,0,0,0,0,0,0,0,0,3000000000,3000000000,3000000000,3000000000,
  //   3000000000,3000000000,3000000000,3000000000,3000000000,3000000000,3000000000,3000000000,
  //   3000000000,3000000000,3000000000,3000000000,1900000969,14000012f,10000060e,120000972,
  //   14000a000,1000000cf,10000060e,220001166,0,0,0,0,0,0,0,0,3000000000,3000000000,3000000000,
  //   3000000000,3000000000,3000000000,3000000000,3000000000,3000000000,3000000000,3000000000,
  //   3000000000,3000000000,3000000000,3000000000,3000000000,1900000969,1800081c0,100001566,
  //   20000a000,0,0,0,0,0,0,0,0,0,0,0,0,3000000000,3000000000,3000000000,3000000000,3000000000,
  //   3000000000,3000000000,3000000000,3000000000,3000000000,3000000000,3000000000,3000000000,
  //   3000000000,3000000000,3000000000,1900000969,14000a000,1000000000,0,0,0,0,0,0,0,0,
  //   0,0,0,0,0,3000000000,3000000000,3000000000,3000000000,3000000000,3000000000,3000000000,
  //   3000000000,3000000000,3000000000,3000000000,3000000000,3000000000,3000000000,3000000000,
  //   3000000000,1900000969,1800081c0,100001566,20000a000,0,0,0,0,0,0,0,0,0,0,0,0,3000000000,
  //   3000000000,3000000000,3000000000,3000000000,3000000000,3000000000,3000000000,3000000000,
  //   3000000000,3000000000,3000000000,3000000000,3000000000,3000000000,3000000000,1900000969,
  //   14000012f,10000060e,120000972,14000a000,1000000cf,10000060e,220001166,0,0,0,0,0,0,
  //   0,0,3000000000,3000000000,3000000000,3000000000,3000000000,3000000000,3000000000,
  //   3000000000,3000000000,3000000000,3000000000,3000000000,3000000000,3000000000,3000000000,
  //   3000000000,1900000969,1800081c0,100001566,20000a000,0,0,0,0,0,0,0,0,0,0,0,0,3000000000,
  //   3000000000,3000000000,3000000000,3000000000,3000000000,3000000000,3000000000,3000000000,
  //   3000000000,3000000000,3000000000,3000000000,3000000000,3000000000,3000000000,1900000969,
  //   14000012f,10000060e,120000972,14000a000,1000000cf,10000060e,220001166,0,0,0,0,0,0,
  //   0,0,3000000000,3000000000,3000000000,3000000000,3000000000,3000000000,3000000000,
  //   3000000000,3000000000,3000000000,3000000000,3000000000,3000000000,3000000000,3000000000,
  //   3000000000,1900000969,1800081c0,100001566,20000a000,0,0,0,0,0,0,0,0,0,0,0,0,3000000000,
  //   3000000000,3000000000,3000000000,3000000000,3000000000,3000000000,3000000000,3000000000,
  //   3000000000,3000000000,3000000000,3000000000,3000000000,3000000000,3000000000,1900000969,
  //   14000012f,10000060e,120000972,14000a000,1000000cf,10000060e,220001166,0,0,0,0,0,0,
  //   0,0,3000000000,3000000000,3000000000,3000000000,3000000000,3000000000,3000000000,
  //   3000000000,3000000000,3000000000,3000000000,3000000000,3000000000,3000000000,3000000000,
  //   3000000000,1900000969,1800081c0,100001566,20000a000,0,0,0,0,0,0,0,0,0,0,0,0,3000000000,
  //   3000000000,3000000000,3000000000,3000000000,3000000000,3000000000,3000000000,3000000000,
  //   3000000000,3000000000,3000000000,3000000000,3000000000,3000000000,3000000000,1900000969,
  //   0,0,0,0,0,0,0,0,0,0,0,0,0,0,0,3000000000,3000000000,3000000000,3000000000,3000000000,
  //   3000000000,3000000000,3000000000,3000000000,3000000000,3000000000,3000000000,3000000000,
  //   3000000000,3000000000,3000000000,1900000969,1800081c0,100001566,20000a000,0,0,0,0,
  //   0,0,0,0,0,0,0,0,3000000000,3000000000,3000000000,3000000000,3000000000,3000000000,
  //   3000000000,3000000000,3000000000,3000000000,3000000000,3000000000,3000000000,3000000000,
  //   3000000000,3000000000,1900000969,14000012f,10000060e,120000972,14000a000,1000000cf,
  //   10000060e,220001166,0,0,0,0,0,0,0,0,3000000000,3000000000,3000000000,3000000000,3000000000,
  //   3000000000,3000000000,3000000000,3000000000,3000000000,3000000000,3000000000,3000000000,
  //   3000000000,3000000000,3000000000,1900000969,1800081c0,100001566,20000a000,0,0,0,0,
  //   0,0,0,0,0,0,0,0,3000000000,3000000000,3000000000,3000000000,3000000000,3000000000,
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  //   contents of ROM_16x64k (hex, n*v repeats v):
  //   0,0,0,0,0,0,0,0,0,0,0,0,0,0,0,0,0,0,0,0,0,0,0,0,0,0,0,0,0,0,0,0,0,0,0,0,0,0,0,0,0,
  //   0,0,0,0,0,0,0,0,0,0,0,0,0,0,0,0,0,0,0,0,0,0,0,0,0,0,0,0,0,0,0,0,0,0,0,0,0,0,0,0,0,
  //   0,0,0,0,0,0,0,0,0,0,0,0,0,0,0,0,0,0,0,0,0,0,0,0,0,0,0,0,0,0,0,0,0,0,0,0,0,0,0,0,0,
  //   0,0,0,0,0,0,0,0,0,0,0,0,0,0,0,0,0,0,0,0,0,0,0,0,0,0,0,0,0,0,0,0,0,0,0,0,0,0,0,0,0,
  //   0,0,0,0,0,0,0,0,0,0,0,0,0,0,0,0,0,0,0,0,0,0,0,0,0,0,0,0,0,0,0,0,0,0,0,0,0,0,0,0,0,
  //   0,0,0,0,0,0,0,0,0,0,0,0,0,0,0,0,0,0,0,0,0,0,0,0,0,0,0,0,0,0,0,0,0,0,0,0,0,0,0,0,0,
  //   0,0,0,0,0,0,0,0,0,0,0,0,0,0,0,0,0,0,0,0,0,0,0,0,0,0,0,0,0,0,0,0,0,0,0,0,0,0,0,0,0,
  //   0,0,0,0,0,0,0,0,0,0,0,0,0,0,0,0,0,0,0,0,0,0,0,0,0,0,0,0,0,0,0,0,0,0,0,0,0,0,0,0,0,
  //   0,0,0,0,0,0,0,0,0,0,0,0,0,0,0,0,0,0,0,0,0,0,0,0,0,0,0,0,0,0,0,0,0,0,0,0,0,0,0,0,0,
  //   0,0,0,0,0,0,0,0,0,0,0,0,0,0,0,0,0,0,0,0,0,0,0,0,0,0,0,0,0,0,0,0,0,0,0,0,0,0,0,0,0,
  //   0,0,0,0,0,0,0,0,0,0,0,0,0,0,0,0,0,0,0,0,0,0,0,0,0,0,0,0,0,0,0,0,0,0,0,0,0,0,0,0,0,
  //   0,0,0,0,0,0,0,0,0,0,0,0,0,0,0,0,0,0,0,0,0,0,0,0,0,0,0,0,0,0,0,0,0,0,0,0,0,0,0,0,0,
  //   0,0,0,0,0,0,0,0,0,0,0,0,0,0,0,0,0,0,0,0,0,0,0,0,0,0,0,0,0,0,0,0,0,0,0,0,0,0,0,0,0,
  //   0,0,0,0,0,0,0,0,0,0,0,0,0,0,0,0,0,0,0,0,0,0,0,0,0,0,0,0,0,0,0,0,0,0,0,0,0,0,0,0,0,
  //   0,0,0,0,0,0,0,0,0,0,0,0,0,0,0,0,0,0,0,0,0,0,0,0,0,0,0,0,0,0,0,0,0,0,0,0,0,0,0,0,0,
  //   0,0,0,0,0,0,0,0,0,0,0,0,0,0,0,0,0,0,0,0,0,0,0,0,0,0,0,0,0,0,0,0,0,0,0,0,0,0,0,0,0,
  //   0,0,0,0,0,0,0,0,0,0,0,0,0,0,0,0,0,0,0,0,0,0,0,0,0,0,0,0,0,0,0,0,0,0,0,0,0,0,0,0,0,
  //   0,0,0,0,0,0,0,0,0,0,0,0,0,0,0,0,0,0,0,0,0,0,0,0,0,0,0,0,0,0,0,0,0,0,0,0,0,0,0,0,0,
  //   0,0,0,0,0,0,0,0,0,0,0,0,0,0,0,0,0,0,0,0,0,0,0,0,0,0,0,0,0,0,0,0,0,0,0,0,0,0,0,0,0,
  //   0,0,0,0,0,0,0,0,0,0,0,0,0,0,0,0,0,0,0,0,0,0,0,0,0,0,0,0,0,0,0,0,0,0,0,0,0,0,0,0,0,
  //   0,0,0,0,0,0,0,0,0,0,0,0,0,0,0,0,0,0,0,0,0,0,0,0,0,0,0,0,0,0,0,0,0,0,0,0,0,0,0,0,0,
  //   0,0,0,0,0,0,0,0,0,0,0,0,0,0,0,0,0,0,0,0,0,0,0,0,0,0,0,0,0,0,0,0,0,0,0,0,0,0,0,0,0,
  //   0,0,0,0,0,0,0,0,0,0,0,0,0,0,0,0,0,0,0,0,0,0,0,0,0,0,0,0,0,0,0,0,0,0,0,0,0,0,0,0,0,
  //   0,0,0,0,0,0,0,0,0,0,0,0,0,0,0,0,0,0,0,0,0,0,0,0,0,0,0,0,0,0,0,0,0,0,0,0,0,0,0,0,0,
  //   0,0,0,0,0,0,0,0,0,0,0,0,0,0,0,0,0,0,0,0,0,0,0,0,0,0,0,0,0,0,0,0,0,0,0,0,0,0,0,0,0,
  //   0,0,0,0,0,0,0,0,0,0,0,0,0,0,0,0,0,0,0,0,0,0,0,0,0,0,0,0,0,0,0,0,0,0,0,0,0,0,0,0,0,
  //   0,0,0,0,0,0,0,0,0,0,0,0,0,0,0,0,0,0,0,0,0,0,0,0,0,0,0,0,0,0,0,0,0,0,0,0,0,0,0,0,0,
  //   0,0,0,0,0,0,0,0,0,0,0,0,0,0,0,0,0,0,0,0,0,0,0,0,0,0,0,0,0,0,0,0,0,0,0,0,0,0,0,0,0,
  //   0,0,0,0,0,0,0,0,0,0,0,0,0,0,0,0,0,0,0,0,0,0,0,0,0,0,0,0,0,0,0,0,0,0,0,0,0,0,0,0,0,
  //   0,0,0,0,0,0,0,0,0,0,0,0,0,0,0,0,0,0,0,0,0,0,0,0,0,0,0,0,0,0,0,0,0,0,0,0,0,0,0,0,0,
  //   0,0,0,0,0,0,0,0,0,0,0,0,0,0,0,0,0,0,0,0,0,0,0,0,0,0,0,0,0,0,0,0,0,0,0,0,0,0,0,0,0,
  //   0,0,0,0,0,0,0,0,0,0,0,0,0,0,0,0,0,0,0,0,0,0,0,0,0,0,0,0,0,0,0,0,0,0,0,0,0,0,0,0,0,
  //   0,0,0,0,0,0,0,0,0,0,0,0,0,0,0,0,0,0,0,0,0,0,0,0,0,0,0,0,0,0,0,0,0,0,0,0,0,0,0,0,0,
  //   0,0,0,0,0,0,0,0,0,0,0,0,0,0,0,0,0,0,0,0,0,0,0,0,0,0,0,0,0,0,0,0,0,0,0,0,0,0,0,0,0,
  //   0,0,0,0,0,0,0,0,0,0,0,0,0,0,0,0,0,0,0,0,0,0,0,0,0,0,0,0,0,0,0,0,0,0,0,0,0,0,0,0,0,
  //   0,0,0,0,0,0,0,0,0,0,0,0,0,0,0,0,0,0,0,0,0,0,0,0,0,0,0,0,0,0,0,0,0,0,0,0,0,0,0,0,0,
  //   0,0,0,0,0,0,0,0,0,0,0,0,0,0,0,0,0,0,0,0,0,0,0,0,0,0,0,0,0,0,0,0,0,0,0,0,0,0,0,0,0,
  //   0,0,0,0,0,0,0,0,0,0,0,0,0,0,0,0,0,0,0,0,0,0,0,0,0,0,0,0,0,0,0,0,0,0,0,0,0,0,0,0,0,
  //   0,0,0,0,0,0,0,0,0,0,0,0,0,0,0,0,0,0,0,0,0,0,0,0,0,0,0,0,0,0,0,0,0,0,0,0,0,0,0,0,0,
  //   0,0,0,0,0,0,0,0,0,0,0,0,0,0,0,0,0,0,0,0,0,0,0,0,0,0,0,0,0,0,0,0,0,0,0,0,0,0,0,0,0,
  //   0,0,0,0,0,0,0,0,0,0,0,0,0,0,0,0,0,0,0,0,0,0,0,0,0,0,0,0,0,0,0,0,0,0,0,0,0,0,0,0,0,
  //   0,0,0,0,0,0,0,0,0,0,0,0,0,0,0,0,0,0,0,0,0,0,0,0,0,0,0,0,0,0,0,0,0,0,0,0,0,0,0,0,0,
  //   0,0,0,0,0,0,0,0,0,0,0,0,0,0,0,0,0,0,0,0,0,0,0,0,0,0,0,0,0,0,0,0,0,0,0,0,0,0,0,0,0,
  //   0,0,0,0,0,0,0,0,0,0,0,0,0,0,0,0,0,0,0,0,0,0,0,0,0,0,0,0,0,0,0,0,0,0,0,0,0,0,0,0,0,
  //   0,0,0,0,0,0,0,0,0,0,0,0,0,0,0,0,0,0,0,0,0,0,0,0,0,0,0,0,0,0,0,0,0,0,0,0,0,0,0,0,0,
  //   0,0,0,0,0,0,0,0,0,0,0,0,0,0,0,0,0,0,0,0,0,0,0,0,0,0,0,0,0,0,0,0,0,0,0,0,0,0,0,0,0,
  //   0,0,0,0,0,0,0,0,0,0,0,0,0,0,0,0,0,0,0,0,0,0,0,0,0,0,0,0,0,0,0,0,0,0,0,0,0,0,0,0,0,
  //   0,0,0,0,0,0,0,0,0,0,0,0,0,0,0,0,0,0,0,0,0,0,0,0,0,0,0,0,0,0,0,0,0,0,0,0,0,0,0,0,0,
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  //   ALU
  //   Registers
  //   Control Panel
  //   ATLAS CPU-16
  //   By Hayden B.
endmodule
